# Fritzing sketch led_red_green_button (saved by Fritzing 0.9.2b)
breadboards: 1

parts:
  Bauteil1 = Arduino Uno (Rev3)
  S1 = Pushbutton [package="[THT]"]
  R1 = Resistor [tolerance=±5% resistance=220 package=THT]
  R2 = Resistor [tolerance=±5% resistance=220 package=THT]
  LED1 = LED - 5mm [color="Red (633nm)" package="5 mm [THT]"]
  LED2 = LED - 5mm [color="Green (570nm)" package="5 mm [THT]"]
  R3 = Resistor [tolerance=±5% resistance=10k package=THT]

nets:
  N1: Bauteil1.D9_PWM, S1.Pin_3, S1.Pin_4, R3.Pin_1
  N2: Bauteil1.D10_PWM/SS, R2.Pin_0
  N3: Bauteil1.D11_PWM/MOSI, R1.Pin_0
  N4: Bauteil1.GND, LED1.cathode, LED2.cathode, R3.Pin_0
  N5: Bauteil1.5V, S1.Pin_1, S1.Pin_2
  N6: R1.Pin_1, LED1.anode
  N7: R2.Pin_1, LED2.anode
