# Fritzing sketch LED_ten_times (saved by Fritzing 0.9.2b)

parts:
  Bauteil1 = Arduino Uno (Rev3)
  LED1 = LED - 5mm [color="Red (633nm)" package="5 mm [THT]"]

nets:
  N1: Bauteil1.D13/SCK, LED1.anode
  N2: Bauteil1.GND, LED1.cathode

notes:
  Der Arduino verfügt über eine LED auf dem Board, der Aufbau mit einer zweiten ist also rein optional.
